# Fritzing sketch ESProject (saved by Fritzing 0.9.3b)
breadboards: 1

parts:
  LCD1 = LCD screen
  Part1 = Arduino Uno (Rev3)
  Part2 = Arduino Uno (Rev3)
  R1 = TRIMPOT [package=3386u]
  S1 = Pushbutton [package="[THT]"]
  S2 = Pushbutton [package="[THT]"]
  S3 = Pushbutton [package="[THT]"]
  Part3 = Digital Temperature Sensor Breakout - TMP102
  R2 = Resistor [tolerance=±5% resistance=10k package="0402 [SMD]"]

nets:
  GND: LCD1.VSS, LCD1.R/W, Part1.GND, Part2.GND, R1.CCW, S1.Pin_3, S1.Pin_4, S2.Pin_3, S2.Pin_4, S3.Pin_3, S3.Pin_4, Part3.GND
  VDD: LCD1.VDD, Part1.5V, R1.CW
  N1: LCD1.V0, R1.WIPER
  N2: LCD1.RS, Part1.A0
  N3: LCD1.E, Part1.A1
  N4: LCD1.DB4, Part1.A2
  N5: LCD1.DB5, Part1.A3
  N6: LCD1.DB6, Part1.A4/SDA, Part3.SDA
  N7: LCD1.DB7, Part1.A5/SCL, Part3.V+
  N8: Part1.AREF, Part3.SCL
  N9: Part1.D0/RX, Part2.D3_PWM
  N10: Part1.D1/TX, Part2.D2, R2.Pin_1
  N11: Part1.D3_PWM, S1.Pin_1, S1.Pin_2
  N12: Part1.D4, S2.Pin_1, S2.Pin_2
  N13: Part1.D6_PWM, S3.Pin_1, S3.Pin_2
  N14: Part1.3V3, R2.Pin_0
